# Fritzing sketch Button (saved by Fritzing 0.9.3b)
breadboards: 1

parts:
  Button = Arduino Uno (Rev3)
  Button_2 = Pushbutton [package="[THT]"]

nets:
  N1: Button.D8, Button_2.Pin_1, Button_2.Pin_2
  N2: Button.GND, Button_2.Pin_3, Button_2.Pin_4
