# Fritzing sketch LCD (saved by Fritzing 0.9.3b)
breadboards: 1

parts:
  LCD = Arduino Uno (Rev3)
  LCD_2 = LCD screen
  R2 = Resistor [tolerance=±5% resistance=220 package="1206 [SMD]"]
  Potentiometer = Rotary Potentiometer (Large) [maximum_resistance=100kΩ package=THT]

nets:
  N1: LCD.D9_PWM, LCD_2.E
  N2: LCD.D12/MISO, LCD_2.RS
  N3: LCD.D2, LCD_2.DB7
  N4: LCD.D4, LCD_2.DB5
  N5: LCD.D5_PWM, LCD_2.DB4
  N6: LCD.D6_PWM, LCD_2.DB6
  5V: LCD.5V, LCD_2.VDD, R2.Pin_1, Potentiometer.leg1
  GND: LCD.GND, LCD_2.VSS, LCD_2.R/W, LCD_2.LED-, Potentiometer.leg2
  N7: LCD_2.V0, Potentiometer.wiper
  N8: LCD_2.LED+, R2.Pin_0
