# Fritzing sketch LED (saved by Fritzing 0.9.3b)
breadboards: 1

parts:
  LED_schematic = Arduino Uno (Rev3)
  LED = LED - 5mm [color="Red (633nm)" package="5 mm [THT]"]
  R1 = Resistor [tolerance=±5% resistance=220 package="1206 [SMD]"]

nets:
  N1: LED_schematic.D13/SCK, LED.anode
  N2: LED_schematic.GND, R1.Pin_0
  N3: LED.cathode, R1.Pin_1
